# Fritzing sketch esp8266-Philips-RC6-tv-remote (saved by Fritzing 0.9.3b)
breadboards: 1

parts:
  WeMos_D1_Mini1 = WeMos D1 Mini
  IR1 = TSOP312.., 314.. [part_number=TSOP38238 package=THT]
  Q1 = NPN-Transistor [part_number=2N3904 package="TO92 [THT]"]
  S2 = SWITCH-MOMENTARY-2 [package=tactile-pth-12mm]
  LED1 = Infrared LED - 5mm [part_number="5mm IR led 940nm" package="5 mm [THT]"]

nets:
  N1: WeMos_D1_Mini1.3V3, IR1.Vs, LED1.anode
  N2: WeMos_D1_Mini1.D1, IR1.Data
  N3: WeMos_D1_Mini1.D2, S2.1
  N4: WeMos_D1_Mini1.D8, Q1.B
  GND: WeMos_D1_Mini1.G, IR1.GND, Q1.E, S2.2
  N5: Q1.C, LED1.cathode

notes:
  VCC
  GND
  CE
  RST
  DC
  DIN
  CLK
  BL
  to set WiFi config:
  D2 to GND at boot to turn ESP8266 into AP mode.

custom parts:
  Infrared LED - 5mm: A generic infrared LED (~1.2V)
